# Fritzing sketch Plan_der_Verkabelung_Fritzing (saved by Fritzing 0.9.10b)

parts:
  S1 = H-Bridge with L298N
  Bauteil1 = Arduino Uno (Rev3)
  HC-SR04_Sensor_1 = HC-SR04 Ultrasonic Distance Sensor  # not connected
  HC-SR04_Sensor_2 = HC-SR04 Ultrasonic Distance Sensor  # not connected
  J1 = Basic Servo  # not connected
  VCC1 = Battery block 9V
  U1 = SWITCH_SPDT [package=kps-1290]
  M1 = DC Motor [voltage_(max)=6V voltage_(min)=3V]
  S2 = Pushbutton [package="[THT]"]  # not connected

nets:
  N1: S1.12V, VCC1.+
  GND: S1.GND, Bauteil1.GND, VCC1.-
  5V: S1.5V, Bauteil1.VIN
  N2: S1.ENA, S1.ENA-5V
  N3: S1.M1-01, M1.pin_2
  N4: S1.M1-02, U1.P

custom parts:
  H-Bridge with L298N: h-bridge
