# Fritzing sketch Plan_der_Verkabelung_Fritzing (saved by Fritzing 0.9.10b)

parts:
  S1 = H-Bridge with L298N
  Bauteil1 = Arduino Uno (Rev3)
  HC-SR04_Sensor_1 = HC-SR04 Ultrasonic Distance Sensor
  HC-SR04_Sensor_2 = HC-SR04 Ultrasonic Distance Sensor
  U1 = SWITCH_SPDT [package=kps-1290]
  S2 = Pushbutton [package="[THT]"]  # not connected
  J1 = Basic Servo  # not connected
  M1 = DC Motor [voltage_(max)=6V voltage_(min)=3V]
  VCC1 = Battery block 9V

nets:
  N1: S1.12V, VCC1.+
  GND: S1.GND, Bauteil1.GND, VCC1.-
  5V: S1.5V, Bauteil1.5V
  N2: S1.ENA, S1.ENA-5V
  N3: S1.IN1, Bauteil1.D2
  N4: S1.IN2, Bauteil1.D3_PWM
  N5: S1.M1-01, M1.pin_2
  N6: S1.M1-02, U1.P
  N7: Bauteil1.D4, HC-SR04_Sensor_1.TRIG
  N8: Bauteil1.D5_PWM, HC-SR04_Sensor_1.ECHO
  N9: Bauteil1.D6_PWM, HC-SR04_Sensor_2.TRIG
  N10: Bauteil1.D7, HC-SR04_Sensor_2.ECHO

custom parts:
  H-Bridge with L298N: h-bridge
